// Logisim project Smart_Tank_Final.circ as structural Verilog: 2 circuits, main circuit main
module main (
  input  S0,
  input  L1,
  input  S1,
  input  FULL,
  input  PUMP,
  input  S2,
  input  L0,
  input  S3,
  input  ALARM,
  input  CLOCK,
  input  RESET
);

  wire and_1_out, and_2_out, and_3_out, d_ff_1_q, d_ff_2_q, d_ff_3_qn, d_ff_4_qn, n7447_1_pin1, n7447_1_pin2,
       n7447_1_pin3, n7447_1_pin7, n7447_1_pin9, n7447_1_pin10, n7447_1_pin11, n7447_1_pin12, n7447_1_pin13,
       n7447_1_pin14, n7447_1_pin15, not_1_out, or_1_out, or_2_out;

  _7447 u_7447_1 (
    .pin1(n7447_1_pin1), .pin2(n7447_1_pin2), .pin3(n7447_1_pin3), .pin4(n7447_1_pin3), .pin5(n7447_1_pin3),
    .pin6(n7447_1_pin2), .pin7(n7447_1_pin7), .pin15(n7447_1_pin15), .pin14(n7447_1_pin14),
    .pin13(n7447_1_pin13), .pin12(n7447_1_pin12), .pin11(n7447_1_pin11), .pin10(n7447_1_pin10),
    .pin9(n7447_1_pin9));
  or or_1 (or_1_out, S3, S2);
  or or_2 (or_2_out, S1, S3);
  _7_Segment_Display u_7_segment_display_1 (
    .g(n7447_1_pin14), .f(n7447_1_pin15), .a(n7447_1_pin13), .b(n7447_1_pin12), .e(n7447_1_pin9),
    .d(n7447_1_pin10), .c(n7447_1_pin11));  // open: dp
  D_Flip_Flop d_ff_1 (.D(L1), .clk(CLOCK), .Q(d_ff_1_q), .reset(RESET));  // open: Qn, preset
  D_Flip_Flop d_ff_2 (.D(L0), .clk(CLOCK), .Q(d_ff_2_q), .reset(RESET));  // open: Qn, preset
  D_Flip_Flop d_ff_3 (
    .D(d_ff_3_qn), .clk(n7447_1_pin7), .Q(n7447_1_pin1), .Qn(d_ff_3_qn), .reset(RESET));  // open: preset
  and and_1 (and_1_out, d_ff_1_q, d_ff_2_q);
  D_Flip_Flop d_ff_4 (.D(d_ff_4_qn), .clk(and_2_out), .Q(n7447_1_pin7), .Qn(d_ff_4_qn), .reset(RESET));  // open: preset
  not not_1 (not_1_out, FULL);
  and and_2 (and_2_out, and_1_out, CLOCK);
  and and_3 (and_3_out, n7447_1_pin7, n7447_1_pin1);
  // also tied to GND on the sheet: n7447_1_pin2
  // also tied to VCC on the sheet: n7447_1_pin3
endmodule

module TruthTable_Test (
  input  S1,
  input  S2,
  input  S3,
  output L1,
  output FULL,
  output PUMP,
  output L0
);

  or or_1 (L1, S3, S2);
  or or_2 (L0, S1, S3);
  and and_1 (FULL, L1, L0);
  not not_1 (PUMP, FULL);
endmodule
